# Fritzing sketch reach_task_circuit (saved by Fritzing 0.9.5d)
breadboards: 2

parts:
  A1 = Teensy 4.1
  Part1 = Audio FX Sound Board + 2x2W Amp
  Part2 = Adafruit MPR121
  M1 = IR break beam 3mm tx [package=THT]
  M2 = IR break beam 3mm rx [package=THT]
  SPKR1 = Loudspeaker
  Q1 = Basic FET N-Channel [package="TO220 [THT]"]
  L1 = Solenoid
  L2 = Solenoid
  L3 = Solenoid
  R1 = Resistor [tolerance=±5% resistance=10k package=THT]
  D1 = Diode [package=diode-hv]
  Q2 = Basic FET N-Channel [package="TO220 [THT]"]
  R2 = Resistor [tolerance=±5% resistance=10k package=THT]
  D2 = Diode [package=diode-hv]
  LED1 = smd LED [color="Red (633nm)" package="0805 [SMD]"]
  R3 = Resistor [tolerance=±5% resistance=220 package="0402 [SMD]"]  # not connected
  R4 = Resistor [tolerance=±5% resistance=220 package="0402 [SMD]"]
  LED2 = smd LED [color="Red (633nm)" package="0805 [SMD]"]
  Q3 = Basic FET N-Channel [package="TO220 [THT]"]
  R5 = Resistor [tolerance=±5% resistance=10k package=THT]
  D3 = Diode [package=diode-hv]
  S1 = Pushbutton [package="[SMD]"]
  R6 = Resistor [tolerance=±5% resistance=10k package="0402 [SMD]"]
  M3 = IR break beam 3mm rx [package=THT]
  M4 = IR break beam 3mm tx [package=THT]

nets:
  GND: A1.Pin_12, A1.Pin_38, A1.Pin_50, A1.Pin_63, Part1.GND, Part1.UG, Part2.GND, M1.pin2, M2.pin3, Q1.source, Q2.source, LED1.cathode, LED2.cathode, Q3.source, R6.Pin_1, M3.pin3, M4.pin2
  N1: A1.Pin_13, Part1.TX
  N2: A1.Pin_14, Part1.RX
  N3: A1.Pin_15, M2.pin2
  N4: A1.Pin_16, M3.pin2
  N5: A1.Pin_21, R4.Pin_0
  N6: A1.Pin_26, A1.Pin_62
  N7: A1.Pin_30, S1.Pin_1, S1.Pin_2, R6.Pin_0
  N8: A1.Pin_32, R5.Pin_0
  N9: A1.Pin_34, R1.Pin_0
  N10: A1.Pin_35, R2.Pin_0
  N11: A1.Pin_56, Part2.SDA
  N12: A1.Pin_57, Part2.SCL
  N13: A1.Pin_59, Part1.RST
  N14: A1.Pin_64, Part2.VIN, M1.pin1, M2.pin1, L1.pin2, L2.pin2, L3.pin2, D1.C, D2.C, D3.C, S1.Pin_3, S1.Pin_4, M3.pin1, M4.pin1
  N15: Part1.L-, SPKR1.pin2
  N16: Part1.L+, SPKR1.pin1
  N17: Q1.gate, R1.Pin_1
  N18: Q1.drain, L1.pin1
  N19: L2.pin1, Q2.drain
  N20: L3.pin1, Q3.drain
  N21: Q2.gate, R2.Pin_1
  N22: R4.Pin_1, LED2.anode
  N23: Q3.gate, R5.Pin_1

notes:
  Right, Left, Vacuum
  Solenoids
  Beam Breaks
  cue LEDs

custom parts:
  Teensy 4.1: The Teensy is a complete USB-based microcontoller development system, in a very small footprint, capable of implementing many types of projects. All programming is done via the USB port. No special programmer is needed, only a standard micro-USB cable and a PC or Macintosh with a USB port.
  Audio FX Sound Board + 2x2W Amp: The Adafruit Sound Board, the fastest way to add audio effects to a project!
  Adafruit MPR121: Add lots of touch sensors to your next microcontroller project with this easy-to-use 12-channel capacitive touch sensor breakout board, starring the MPR121. This chip can handle up to 12 individual touch pads. The MPR121 has support for only I2C, which can be implemented with nearly any microcontroller. You can select one of 4 addresses with the ADDR pin, for a total of 48 capacitive touch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
  IR break beam 3mm tx: Infrared break beam Sensor tx module.
  IR break beam 3mm rx: Infrared break beam Sensor rx module.
